# Fritzing sketch ElectronicFocus (saved by Fritzing 0.9.3b)
breadboards: 2

parts:
  Part1 = EasyDriver_v44
  Part2 = Arduino Nano (Rev3.0)
  M1 = Stepper Motor - Bipolar
  S1 = Pushbutton [package="[THT]"]
  R1 = Rotary Potentiometer (Small) [maximum_resistance=100kΩ package=THT]
  S4 = SPST Switch [package=switche-dpdt]
  J1 = Power Jack [package=power_jack_combo]
  LED1 = smd LED [color="Red (633nm)" package="1206 [SMD]"]
  R2 = Resistor [tolerance=±5% resistance=220 package="0805 [SMD]"]
  S5 = SPST Switch [package=switche-dpdt]
  C1 = Electrolytic Capacitor [capacitance=10μF voltage=20V package="0605 [SMD, electrolytic]"]

nets:
  GND: Part1.GND, Part2.GND, S1.Pin_1, R1.leg1, S4.O, LED1.cathode, C1.-
  N1: Part1.V+, Part2.VIN, S5.P, C1.+
  N2: Part1.STEP, Part2.D3
  N3: Part1.DIR, Part2.D2
  N4: Part1.OUT2A, M1.A
  N5: Part1.OUT2B, M1.C
  N6: Part1.OUT1A, M1.B
  N7: Part1.OUT1B, M1.D
  N8: Part1.MS1, Part2.D4
  N9: Part1.ENABLE, Part2.D6
  N10: Part1.MS2, Part2.D5
  N11: Part2.D7, S1.Pin_3
  N12: Part2.D8, S4.P
  N13: Part2.D9, R2.Pin_1
  N14: Part2.A0, R1.wiper
  N15: Part2.3V3, R1.leg2, S4.S
  N16: J1.PWR, S5.O
  N17: LED1.anode, R2.Pin_0

notes:
  The higher the input voltage, the less current can be draw to other components??
  Jeg tror, rundt 7v opp til 2.5A vil være ok? DC.
  Jo mere componenter jeg har ut av arduino, desto mer AMP trenger jeg?
  7-21v, rundt 300-500mA
  0.33A max (per coil?)
  6-30v, up to 2A
  Motor bit?
  2.1mm x 5mm DC jack
  Pluggen må tåle nok spenning.

// code stored in the sketch: ElectronicFocus.ino
#define DIR 2
#define STEP 3
#define MS1 4
#define MS2 5
#define EN 6
#define BTN_START 7
#define DIR_SWITCH 8
#define LED 9
#define POT_SPEED 0


void setup() {
	
	//  Motor	
	pinMode(DIR, OUTPUT);
	pinMode(STEP, OUTPUT);
	pinMode(MS1, OUTPUT);
	pinMode(MS2, OUTPUT);
	pinMode(EN, OUTPUT);
	pinMode(LED, OUTPUT);
	initPins();
	
	// Motor Controls
	pinMode(BTN_START, INPUT_PULLUP);
	pinMode(DIR_SWITCH, INPUT);

}


void loop() {

	// set the direction of the motor based on the switch state, ON == forward, OFF == backward
	// set the speed of the motor based on the POT signal.
	// set actually move the motor if the the button is HIGH

}


void initPins() { // set default states
	digitalWrite(DIR, LOW);
	digitalWrite(STEP, LOW);
	digitalWrite(MS1, LOW);
	digitalWrite(MS2, LOW);
	digitalWrite(EN, HIGH);
	digitalWrite(LED, HIGH);
}
