# Fritzing sketch MotorArduinoNanoTest (saved by Fritzing 0.9.3b)
breadboards: 1

parts:
  Part1 = EasyDriver_v44
  Part2 = Arduino Nano Every
  M1 = Stepper Motor - Bipolar
  U1 = 2.5mm Audio Jack [package=stereojack2.5mm_specia_pogopins]

nets:
  GND: Part1.GND, Part2.GND, Part2.D13~, U1.RIGHT
  N1: Part1.V+, Part2.VIN, U1.LEFT
  N2: Part1.STEP, Part2.D5~
  N3: Part1.DIR, Part2.D6~
  N4: Part1.OUT2A, M1.A
  N5: Part1.OUT2B, M1.C
  N6: Part1.OUT1A, M1.B
  N7: Part1.OUT1B, M1.D
  N8: Part1.MS1, Part2.D7
  N9: Part1.ENABLE, Part2.D9~
  N10: Part1.MS2, Part2.D8
  N11: Part2.RESET, Part2.A7
  N12: Part2.D11/MOSI, Part2.+5V

notes:
  12v 3A

custom parts:
  Arduino Nano Every: The Nano Every is Arduino’s 5V compatible board in the smallest available form factor: 45x18mm! The Arduino Nano is the preferred board for many projects requiring a small and easy to use microcontroller board. The small footprint and low price, make the Nano Every particularly suited for wearable inventions, low cost robotics, electronic musical instruments, and general use to control smaller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

// code stored in the sketch: MotorArduinoNanoTest.ino
// code from https://learn.sparkfun.com/tutorials/easy-driver-hook-up-guide?_ga=2.39140388.689569295.1626355120-1811491594.1626355120

#define STEP 5
#define DIR 6
#define MS1 7
#define MS2 8
#define ENABLE 9

//declaring vars for functions 
char user_input;
int x;
int y;
int state;

void setup() {
  pinMode(STEP, OUTPUT);
  pinMode(DIR, OUTPUT);
  pinMode(MS1, OUTPUT);
  pinMode(MS2, OUTPUT);
  pinMode(ENABLE, OUTPUT);
  resetEDPins();
  Serial.begin(9600);
  Serial.println("Begin motor control");
  Serial.println();
  Serial.println("Enter number for control option:");
  Serial.println("1. Turn at default microstep mode.");
  Serial.println("2. Reverse direction at default microstep mode.");
  Serial.println("3. Turn at 1/8th microstep mode.");
  Serial.println("4. Step forward and reverse direction.");
  Serial.println();
} 

void loop() {
  while(Serial.available()) {

    user_input = Serial.read();
    digitalWrite(ENABLE, LOW); //pull enable pin to low to allow for motor control
    
    if (user_input == "1") {
      stepforwarddefault(); 
    } else if (user_input == "2") {
      reversestepdefault();
    } else if (user_input == "3") {
      smallstepmode();
    } else if (user_input == "4") {
      forwardbackwardstep();
    } else {
      Serial.println("Invalid option entered..");
    }
    resetEDPins();
  }
}


void stepforwarddefault() {
  Serial.println("Moving forward at default step mode.");
  digitalWrite(DIR, LOW); // pull direction pin low to move "forward"
  for (x=0; x<1000; x++) {
    digitalWrite(STEP, HIGH); // move one forward
    delay(1);
    digitalWrite(STEP, LOW);
    delay(1); 
  }
  Serial.println("Enter new option");
  Serial.println();
}


void reversestepdefault() {
  Serial.println("Moving reverse at default step mode.");
  digitalWrite(DIR, HIGH); // pull direction pin high to move "backward"
  for (x=0; x<1000; x++) {
    digitalWrite(STEP, HIGH); // move one forward
    delay(1);
    digitalWrite(STEP, LOW);
    delay(1); 
  }
  Serial.println("Enter new option");
  Serial.println();
}


void smallstepmode() {
  Serial.println("Stepping at 1/8th microstep mode");
  
  digitalWrite(MS1, HIGH);
  digitalWrite(MS2, HIGH); // set to microstep resolution.

  digitalWrite(DIR, LOW); // pull direction pin low to move "forward"
  for (x=0; x<1000; x++) {
    digitalWrite(STEP, HIGH); // move one forward
    delay(1);
    digitalWrite(STEP, LOW);
    delay(1); 
  }
  Serial.println("Enter new option");
  Serial.println();
}


void forwardbackwardstep() {
  Serial.println("Alternate between stepping forward and reverse");
  for (x=1; x<5; x++) {
    state = digitalRead(DIR);
    if (state == HIGH) {
      digitalWrite(DIR, LOW);
    } else if (state == LOW) {
      digitalWrite(DIR, HIGH);
    }
    for (y=0; y<1000; y++) {
      digitalWrite(STEP, HIGH);
      delay(1);
      digitalWrite(STEP, LOW);
      delay(1);
    }
  }
  Serial.println("Enter new option");
  Serial.println();
}

void resetEDPins() {
  digitalWrite(STEP, LOW);
  digitalWrite(DIR, LOW);
  digitalWrite(MS1, LOW);
  digitalWrite(MS2, LOW);
  digitalWrite(ENABLE, HIGH);
}

// code stored in the sketch: MotorTest.ino
// code from https://learn.sparkfun.com/tutorials/easy-driver-hook-up-guide?_ga=2.39140388.689569295.1626355120-1811491594.1626355120

#define STEP 5
#define DIR 6
#define MS1 7
#define MS2 8
#define ENABLE 9


void setup() {
	pinMode(STEP, OUTPUT);
	pinMode(DIR, OUTPUT);
	pinMode(MS1, OUTPUT);
	pinMode(MS2, OUTPUT);
	pinMode(ENABLE, OUTPUT);
	resetEDPins();
	Serial.begin(9600);
	Serial.println("Begin motor control");
	Serial.println();
	Serial.println("Enter number for control option:");
	Serial.println("1. Turn at default microstep mode.");
	Serial.println("2. Reverse direction at default microstep mode.");
	Serial.println("3. Turn at 1/8th microstep mode.");
	Serial.println("4. Step forward and reverse direction.");
	Serial.println();
} 

void loop() {
	while(Serial.avaliable()) {

		user_input = Serial.read();
		digitalWrite(EN, LOW); //pull enable pin to low to allow for motor control
		
		if (user_input == "1") {
			stepforwarddefault();	
		} else if (user_input == "2") {
			reversestepdefault();
		} else if (user_input == "3") {
			smallstepmode();
		} else if (user_input == "4") {
			forwardbackwardstep();
		} else {
			Serial.println("Invalid option entered..");
		}
		resetEDPins();
	}
}


void stepforwarddefault() {
	Serial.println("Moving forward at default step mode.");
	digitalWrite(DIR, LOW); // pull direction pin low to move "forward"
	for (x=0; x<1000; x++) {
		digitalWrite(STEP, HIGH); // move one forward
		delay(1);
		digitalWrite(STEP, LOW);
		delay(1);	
	}
	Serial.println("Enter new option");
	Serial.println();
}


void reversestepdefault() {
	Serial.println("Moving reverse at default step mode.");
	digitalWrite(DIR, HIGH); // pull direction pin high to move "backward"
	for (x=0; x<1000; x++) {
		digitalWrite(STEP, HIGH); // move one forward
		delay(1);
		digitalWrite(STEP, LOW);
		delay(1);	
	}
	Serial.println("Enter new option");
	Serial.println();
}


void smallstepmode() {
	Serial.println("Stepping at 1/8th microstep mode");
	
	digitalWrite(MS1, HIGH);
	digitalWrite(MS2, HIGH); // set to microstep resolution.

	digitalWrite(DIR, LOW); // pull direction pin low to move "forward"
	for (x=0; x<1000; x++) {
		digitalWrite(STEP, HIGH); // move one forward
		delay(1);
		digitalWrite(STEP, LOW);
		delay(1);	
	}
	Serial.println("Enter new option");
	Serial.println();
}


void forwardbackwardstep() {
	Serial.println("Alternate between stepping forward and reverse");
	for (x=1; x<5; x++) {
		state = digitalRead(DIR);
		if (state == HIGH) {
			digitalWrite(DIR, LOW);
		} else if (state == LOW) {
			digitalWrite(DIR, HIGH);
		}
		for (y=0; y<1000; y++) {
			digitalWrite(STEP, HIGH);
			delay(1);
			digitalWrite(STEP, LOW);
			delay(1);
		}
	}
	Serial.println("Enter new option");
	Serial.println();
}

void resetEDPins() {
	digitalWrite(STEP, LOW);
	digitalWrite(DIR, LOW);
	digitalWrite(MS1, LOW);
	digitalWrite(MS2, LOW);
	digitalWrite(ENABLE, HIGH);

}
