# Fritzing sketch MotorizedTelescopeFocuser (saved by Fritzing 0.9.3b)
breadboards: 2

parts:
  Part4 = EasyDriver_v44
  R4 = Rotary Potentiometer (Small) [maximum_resistance=10kΩ package=THT]
  S6 = Pushbutton [package="[THT]"]
  S7 = SPST Switch [package=switche-dpdt]
  LED2 = smd LED [color="Red (633nm)" package="1206 [SMD]"]
  R5 = Resistor [tolerance=±5% resistance=220 package="0805 [SMD]"]
  R6 = Resistor [tolerance=±5% resistance=4.7k package="0805 [SMD]"]
  Part3 = Arduino Nano Every
  M2 = Stepper Motor - Bipolar
  J2 = Power Jack [package=power_jack_combo]
  S8 = SPST Switch [package=switche-dpdt]

nets:
  GND: Part4.GND, R4.leg1, S6.Pin_1, S6.Pin_2, S7.S, LED2.cathode, R6.Pin_1, Part3.GND, Part3.D13~
  N1: Part4.V+, Part3.VIN, S8.P
  N2: Part4.STEP, Part3.D3~
  N3: Part4.DIR, Part3.D2
  N4: Part4.OUT2A, M2.A
  N5: Part4.OUT2B, M2.C
  N6: Part4.OUT1A, M2.B
  N7: Part4.OUT1B, M2.D
  N8: Part4.MS1, Part3.D4
  N9: Part4.ENABLE, Part3.D6~
  N10: Part4.MS2, Part3.D5~
  N11: R4.wiper, R6.Pin_0, Part3.A0
  N12: R4.leg2, S7.O, Part3.3V3
  N13: S6.Pin_3, S6.Pin_4, Part3.D7
  N14: S7.P, Part3.D8
  N15: LED2.anode, R5.Pin_1
  N16: R5.Pin_0, Part3.D9~
  N17: Part3.RESET, Part3.A7
  N18: Part3.D11/MOSI, Part3.+5V
  N19: J2.PWR, S8.O

notes:
  7-21v, rundt 300-500mA, tror jeg.
  0.33A max (per coil)
  6-30v, up to 2A
  12v 3A

custom parts:
  Arduino Nano Every: The Nano Every is Arduino’s 5V compatible board in the smallest available form factor: 45x18mm! The Arduino Nano is the preferred board for many projects requiring a small and easy to use microcontroller board. The small footprint and low price, make the Nano Every particularly suited for wearable inventions, low cost robotics, electronic musical instruments, and general use to control smaller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

// code stored in the sketch: ElectricFocus.ino
#include <Stepper.h>

#define DIR 2
#define STEP 3
#define MS1 4
#define MS2 5
#define EN 6
#define BTN 7
#define SWITCH 8
#define LED 9
#define POT 0 // 757 - 7

const int STEPS_PER_REV = 200;
unsigned long curr_potval = 1;
boolean motorDir = true;

void setup() {
  // Serial
  Serial.begin(9600);
  
	//  Motor	Driver
	pinMode(DIR, OUTPUT);
	pinMode(STEP, OUTPUT);
	pinMode(MS1, OUTPUT);
	pinMode(MS2, OUTPUT);
	pinMode(EN, OUTPUT);
	pinMode(LED, OUTPUT);
	initPins();
	
	// Motor Controls
	pinMode(BTN, INPUT_PULLUP);
	pinMode(SWITCH, INPUT);

  // Event handler 
  attachInterrupt(digitalPinToInterrupt(SWITCH), changedir, CHANGE);
}

void loop() {
  //curr_potval = map(analogRead(POT), 710, 0, 500, 1); // ???
  Serial.println(analogRead(POT));
  if (!digitalRead(BTN)) {
    digitalWrite(EN, LOW);
    digitalWrite(STEP, HIGH);
    delay(curr_potval);
    digitalWrite(STEP, LOW);
    delay(curr_potval);
    return;
  }
  digitalWrite(EN, HIGH);
}

void changedir() {
  motorDir = !motorDir;
  digitalWrite(DIR, motorDir);
}

void initPins() {
	digitalWrite(DIR, HIGH);
	digitalWrite(STEP, LOW);
	digitalWrite(MS1, LOW);
	digitalWrite(MS2, LOW);
	digitalWrite(EN, HIGH);
	digitalWrite(LED, HIGH);
}

// code stored in the sketch: ElectronicFocus.ino
#define DIR 2
#define STEP 3
#define MS1 4
#define MS2 5
#define EN 6
#define BTN_START 7
#define DIR_SWITCH 8
#define LED 9
#define POT_SPEED 0


void setup() {
	
	//  Motor	
	pinMode(DIR, OUTPUT);
	pinMode(STEP, OUTPUT);
	pinMode(MS1, OUTPUT);
	pinMode(MS2, OUTPUT);
	pinMode(EN, OUTPUT);
	pinMode(LED, OUTPUT);
	initPins();
	
	// Motor Controls
	pinMode(BTN_START, INPUT_PULLUP);
	pinMode(DIR_SWITCH, INPUT);

}


void loop() {

	// set the direction of the motor based on the switch state, ON == forward, OFF == backward
	// set the speed of the motor based on the POT signal.
	// set actually move the motor if the the button is HIGH

}


void initPins() { // set default states
	digitalWrite(DIR, LOW);
	digitalWrite(STEP, LOW);
	digitalWrite(MS1, LOW);
	digitalWrite(MS2, LOW);
	digitalWrite(EN, HIGH);
	digitalWrite(LED, HIGH);
}
